// Logisim project Control Unit.circ as structural Verilog: 1 circuit, main circuit main
module main (
  input  [31:0] Instruction,
  output RegDST,
  output RegWrite,
  output [2:0] out_4,
  output ALUSrc,
  output jump
);

  wire AddI_out, and_1_out, and_2_out, and_3_out, and_6_out, AndI_out, comparator_1_eq, not_1_out, not_2_out,
       not_3_out, not_4_out, not_5_out, not_6_out, not_7_out, not_8_out, not_9_out, not_10_out, not_11_out,
       not_12_out, not_13_out, not_14_out, not_15_out, not_16_out, not_17_out, not_18_out, not_19_out,
       not_20_out, not_21_out, not_22_out, not_23_out, not_24_out, not_25_out, not_26_out, not_27_out,
       not_28_out, not_29_out, not_30_out, not_31_out, not_32_out, not_33_out, not_34_out, not_35_out,
       not_36_out, not_37_out, not_38_out, or_3_out, OrI_out, SubI_out;
  wire [2:0] and_5_out, multiplexer_2_out;

  not not_1 (not_1_out, Instruction[26]);
  not not_2 (not_2_out, Instruction[27]);
  not not_3 (not_3_out, Instruction[28]);
  not not_4 (not_4_out, Instruction[30]);
  not not_5 (not_5_out, Instruction[31]);
  not not_6 (not_6_out, Instruction[27]);
  not not_7 (not_7_out, Instruction[28]);
  not not_8 (not_8_out, Instruction[30]);
  not not_9 (not_9_out, Instruction[31]);
  not not_10 (not_10_out, Instruction[26]);
  not not_11 (not_11_out, Instruction[27]);
  not not_12 (not_12_out, Instruction[30]);
  not not_13 (not_13_out, Instruction[31]);
  not not_14 (not_14_out, Instruction[27]);
  not not_15 (not_15_out, Instruction[30]);
  not not_16 (not_16_out, Instruction[31]);
  not not_17 (not_17_out, Instruction[26]);
  not not_18 (not_18_out, Instruction[28]);
  not not_19 (not_19_out, Instruction[29]);
  not not_20 (not_20_out, Instruction[30]);
  not not_21 (not_21_out, Instruction[31]);
  not not_22 (not_22_out, Instruction[26]);
  not not_23 (not_23_out, Instruction[27]);
  not not_24 (not_24_out, Instruction[28]);
  not not_25 (not_25_out, Instruction[29]);
  not not_26 (not_26_out, Instruction[30]);
  not not_27 (not_27_out, Instruction[31]);
  and R_Type (RegDST, not_22_out, not_23_out, not_24_out, not_25_out, not_26_out, not_27_out);
  and AddI (AddI_out, not_1_out, not_2_out, not_3_out, Instruction[29], not_4_out, not_5_out);
  and SubI (SubI_out, Instruction[26], not_6_out, not_7_out, Instruction[29], not_8_out, not_9_out);
  and AndI (AndI_out, not_10_out, not_11_out, Instruction[28], Instruction[29], not_12_out, not_13_out);
  and OrI (OrI_out, Instruction[26], not_14_out, Instruction[28], Instruction[29], not_15_out, not_16_out);
  and J (jump, not_17_out, Instruction[27], not_18_out, not_19_out, not_20_out, not_21_out);
  or or_1 (RegWrite, RegDST, AddI_out, OrI_out, SubI_out, AndI_out);
  or or_2 (ALUSrc, AddI_out, OrI_out, SubI_out, AndI_out);
  not not_28 (not_28_out, Instruction[2]);
  not not_29 (not_29_out, Instruction[1]);
  not not_30 (not_30_out, Instruction[3]);
  not not_31 (not_31_out, Instruction[2]);
  not not_32 (not_32_out, Instruction[4]);
  and and_1 (and_1_out, Instruction[1], not_28_out, not_30_out);
  and and_2 (and_2_out, not_29_out, Instruction[2], not_30_out);
  not not_33 (not_33_out, Instruction[4]);
  not not_34 (not_34_out, Instruction[0]);
  not not_35 (not_35_out, Instruction[1]);
  not not_36 (not_36_out, Instruction[0]);
  or or_3 (or_3_out, and_1_out, and_2_out);
  and and_3 (and_3_out, not_33_out, not_34_out, Instruction[5]);
  not not_37 (not_37_out, Instruction[3]);
  not not_38 (not_38_out, Instruction[4]);
  and and_4 (and_5_out[2], not_36_out, Instruction[1], not_31_out, not_32_out, Instruction[5]);
  and and_5 (and_5_out[0], or_3_out, and_3_out);
  and and_6 (and_6_out, Instruction[0], not_35_out, Instruction[2], not_37_out, not_38_out, Instruction[5]);
  Multiplexer #(.width(3)) multiplexer_1 (
    .in0(Instruction[28:26]), .in1(multiplexer_2_out), .out(out_4), .sel(RegDST));  // open: en
  or or_4 (and_5_out[1], and_5_out[0], and_6_out);
  Comparator #(.width(6)) comparator_1 (.a(6'b011000), .b(Instruction[5:0]), .eq(comparator_1_eq));  // open: gt, lt
  Multiplexer #(.width(3)) multiplexer_2 (
    .in0(and_5_out), .in1(3'b111), .out(multiplexer_2_out), .sel(comparator_1_eq));  // open: en

  // Notes on the sheet:
  //   Opcode
  //   ALU ctr [0]
  //   ALU ctr [2]
  //   ALU ctr [1]
  //   ALU ctr
endmodule
