// Logisim project Data Path design.circ as structural Verilog: 4 circuits, main circuit main
module main (
  input  [31:0] in_1
);

  wire clock_1_out, control_unit_1_alusrc, control_unit_1_jump, control_unit_1_regdst,
       control_unit_1_regwrite;
  wire [2:0] control_unit_1_out_4;
  wire [4:0] multiplexer_1_out;
  wire [31:0] adder_1_out, alu_1_result, bit_extender_1_out, counter_1_q, multiplexer_2_out,
       multiplexer_3_out, registe_file_1_regread1, registe_file_1_regread2;

  Clock clock_1 (.out(clock_1_out));
  Counter #(.width(32), .max('hffffffff)) counter_1 (
    .load(1'b1), .D(multiplexer_2_out), .count(1'b0), .Q(counter_1_q), .clk(clock_1_out));  // open: carry, clr
  Adder #(.width(32)) adder_1 (.a(32'h4), .b(counter_1_q), .out(adder_1_out));  // open: cin, cout
  Multiplexer #(.width(5)) multiplexer_1 (
    .in0(in_1[15:11]), .in1(in_1[20:16]), .out(multiplexer_1_out), .sel(control_unit_1_regdst));  // open: en
  assign bit_extender_1_out = {{16{1'b0}}, in_1[15:0]};  // Bit_Extender bit_extender_1
  Control_Unit control_unit_1 (
    .Instruction(in_1), .RegDST(control_unit_1_regdst), .RegWrite(control_unit_1_regwrite),
    .out_4(control_unit_1_out_4), .ALUSrc(control_unit_1_alusrc), .jump(control_unit_1_jump));
  Registe_File registe_file_1 (
    .dataWrite(alu_1_result), .readNum_1(in_1[20:16]), .readNum_2(in_1[25:21]),
    .regRead1(registe_file_1_regread1), .regRead2(registe_file_1_regread2), .regNum(multiplexer_1_out),
    .regWrite(control_unit_1_regwrite), .in_4(clock_1_out));
  Multiplexer #(.width(32)) multiplexer_2 (
    .in0(adder_1_out), .in1(bit_extender_1_out), .out(multiplexer_2_out), .sel(control_unit_1_jump));  // open: en
  Multiplexer #(.width(32)) multiplexer_3 (
    .in0(registe_file_1_regread1), .in1(bit_extender_1_out), .out(multiplexer_3_out),
    .sel(control_unit_1_alusrc));  // open: en
  ALU alu_1 (
    .Value1(registe_file_1_regread2), .Value2(multiplexer_3_out), .in_3(control_unit_1_out_4),
    .result(alu_1_result));
endmodule

module Registe_File (
  input  [31:0] dataWrite,
  input  [4:0] regNum,
  input  regWrite,
  input  in_4,
  input  [4:0] readNum_1,
  input  [4:0] readNum_2,
  output [31:0] regRead1,
  output [31:0] regRead2
);

  wire and_1_out, and_2_out, and_3_out, and_4_out, and_5_out, and_6_out, and_7_out, and_8_out, and_9_out,
       and_10_out, and_11_out, and_12_out, and_13_out, and_14_out, and_15_out, and_16_out, and_17_out,
       and_18_out, and_19_out, and_20_out, and_21_out, and_22_out, and_23_out, and_24_out, and_25_out,
       and_26_out, and_27_out, and_28_out, and_29_out, and_30_out, and_31_out, and_32_out, decoder_1_out0,
       decoder_1_out1, decoder_1_out2, decoder_1_out3, decoder_1_out4, decoder_1_out5, decoder_1_out6,
       decoder_1_out7, decoder_1_out8, decoder_1_out9, decoder_1_out10, decoder_1_out11, decoder_1_out12,
       decoder_1_out13, decoder_1_out14, decoder_1_out15, decoder_1_out16, decoder_1_out17, decoder_1_out18,
       decoder_1_out19, decoder_1_out20, decoder_1_out21, decoder_1_out22, decoder_1_out23, decoder_1_out24,
       decoder_1_out25, decoder_1_out26, decoder_1_out27, decoder_1_out28, decoder_1_out29, decoder_1_out30,
       decoder_1_out31;
  wire [31:0] register_1_q, register_2_q, register_3_q, register_4_q, register_5_q, register_6_q,
       register_7_q, register_8_q, register_9_q, register_10_q, register_11_q, register_12_q, register_13_q,
       register_14_q, register_15_q, register_16_q, register_17_q, register_18_q, register_19_q,
       register_20_q, register_21_q, register_22_q, register_23_q, register_24_q, register_25_q,
       register_26_q, register_27_q, register_28_q, register_29_q, register_30_q, register_31_q,
       register_32_q;

  Decoder #(.select(5)) decoder_1 (
    .out0(decoder_1_out0), .out1(decoder_1_out1), .out2(decoder_1_out2), .out3(decoder_1_out3),
    .out4(decoder_1_out4), .out5(decoder_1_out5), .out6(decoder_1_out6), .out7(decoder_1_out7),
    .out8(decoder_1_out8), .out9(decoder_1_out9), .out10(decoder_1_out10), .out11(decoder_1_out11),
    .out12(decoder_1_out12), .out13(decoder_1_out13), .out14(decoder_1_out14), .out15(decoder_1_out15),
    .out16(decoder_1_out16), .out17(decoder_1_out17), .out18(decoder_1_out18), .out19(decoder_1_out19),
    .out20(decoder_1_out20), .out21(decoder_1_out21), .out22(decoder_1_out22), .out23(decoder_1_out23),
    .out24(decoder_1_out24), .out25(decoder_1_out25), .out26(decoder_1_out26), .out27(decoder_1_out27),
    .out28(decoder_1_out28), .out29(decoder_1_out29), .out30(decoder_1_out30), .out31(decoder_1_out31),
    .sel(regNum));  // open: en
  and and_1 (and_1_out, regWrite, decoder_1_out0);
  and and_2 (and_2_out, regWrite, decoder_1_out1);
  and and_3 (and_3_out, regWrite, decoder_1_out2);
  and and_4 (and_4_out, regWrite, decoder_1_out3);
  and and_5 (and_5_out, regWrite, decoder_1_out4);
  and and_6 (and_6_out, regWrite, decoder_1_out5);
  and and_7 (and_7_out, regWrite, decoder_1_out6);
  and and_8 (and_8_out, regWrite, decoder_1_out7);
  Register #(.width(32)) register_1 (.D(dataWrite), .en(and_1_out), .Q(register_1_q), .clk(in_4));  // open: clr
  Register #(.width(32)) register_2 (.D(dataWrite), .en(and_2_out), .Q(register_2_q), .clk(in_4));  // open: clr
  Register #(.width(32)) register_3 (.D(dataWrite), .en(and_3_out), .Q(register_3_q), .clk(in_4));  // open: clr
  Register #(.width(32)) register_4 (.D(dataWrite), .en(and_4_out), .Q(register_4_q), .clk(in_4));  // open: clr
  Register #(.width(32)) register_5 (.D(dataWrite), .en(and_5_out), .Q(register_5_q), .clk(in_4));  // open: clr
  Register #(.width(32)) register_6 (.D(dataWrite), .en(and_6_out), .Q(register_6_q), .clk(in_4));  // open: clr
  Register #(.width(32)) register_7 (.D(dataWrite), .en(and_7_out), .Q(register_7_q), .clk(in_4));  // open: clr
  Register #(.width(32)) register_8 (.D(dataWrite), .en(and_8_out), .Q(register_8_q), .clk(in_4));  // open: clr
  and and_9 (and_9_out, regWrite, decoder_1_out8);
  and and_10 (and_10_out, regWrite, decoder_1_out9);
  and and_11 (and_11_out, regWrite, decoder_1_out10);
  and and_12 (and_12_out, regWrite, decoder_1_out11);
  and and_13 (and_13_out, regWrite, decoder_1_out12);
  and and_14 (and_14_out, regWrite, decoder_1_out13);
  and and_15 (and_15_out, regWrite, decoder_1_out14);
  and and_16 (and_16_out, regWrite, decoder_1_out15);
  Register #(.width(32)) register_9 (.D(dataWrite), .en(and_9_out), .Q(register_9_q), .clk(in_4));  // open: clr
  Register #(.width(32)) register_10 (.D(dataWrite), .en(and_10_out), .Q(register_10_q), .clk(in_4));  // open: clr
  Register #(.width(32)) register_11 (.D(dataWrite), .en(and_11_out), .Q(register_11_q), .clk(in_4));  // open: clr
  Register #(.width(32)) register_12 (.D(dataWrite), .en(and_12_out), .Q(register_12_q), .clk(in_4));  // open: clr
  Register #(.width(32)) register_13 (.D(dataWrite), .en(and_13_out), .Q(register_13_q), .clk(in_4));  // open: clr
  Register #(.width(32)) register_14 (.D(dataWrite), .en(and_14_out), .Q(register_14_q), .clk(in_4));  // open: clr
  Register #(.width(32)) register_15 (.D(dataWrite), .en(and_15_out), .Q(register_15_q), .clk(in_4));  // open: clr
  Register #(.width(32)) register_16 (.D(dataWrite), .en(and_16_out), .Q(register_16_q), .clk(in_4));  // open: clr
  and and_17 (and_17_out, regWrite, decoder_1_out16);
  and and_18 (and_18_out, regWrite, decoder_1_out17);
  and and_19 (and_19_out, regWrite, decoder_1_out18);
  and and_20 (and_20_out, regWrite, decoder_1_out19);
  and and_21 (and_21_out, regWrite, decoder_1_out20);
  and and_22 (and_22_out, regWrite, decoder_1_out21);
  and and_23 (and_23_out, regWrite, decoder_1_out22);
  and and_24 (and_24_out, regWrite, decoder_1_out23);
  Register #(.width(32)) register_17 (.D(dataWrite), .en(and_17_out), .Q(register_17_q), .clk(in_4));  // open: clr
  Register #(.width(32)) register_18 (.D(dataWrite), .en(and_18_out), .Q(register_18_q), .clk(in_4));  // open: clr
  Register #(.width(32)) register_19 (.D(dataWrite), .en(and_19_out), .Q(register_19_q), .clk(in_4));  // open: clr
  Register #(.width(32)) register_20 (.D(dataWrite), .en(and_20_out), .Q(register_20_q), .clk(in_4));  // open: clr
  Register #(.width(32)) register_21 (.D(dataWrite), .en(and_21_out), .Q(register_21_q), .clk(in_4));  // open: clr
  Register #(.width(32)) register_22 (.D(dataWrite), .en(and_22_out), .Q(register_22_q), .clk(in_4));  // open: clr
  Register #(.width(32)) register_23 (.D(dataWrite), .en(and_23_out), .Q(register_23_q), .clk(in_4));  // open: clr
  Register #(.width(32)) register_24 (.D(dataWrite), .en(and_24_out), .Q(register_24_q), .clk(in_4));  // open: clr
  and and_25 (and_25_out, regWrite, decoder_1_out24);
  and and_26 (and_26_out, regWrite, decoder_1_out25);
  and and_27 (and_27_out, regWrite, decoder_1_out26);
  and and_28 (and_28_out, regWrite, decoder_1_out27);
  and and_29 (and_29_out, regWrite, decoder_1_out28);
  and and_30 (and_30_out, regWrite, decoder_1_out29);
  and and_31 (and_31_out, regWrite, decoder_1_out30);
  and and_32 (and_32_out, regWrite, decoder_1_out31);
  Register #(.width(32)) register_25 (.D(dataWrite), .en(and_25_out), .Q(register_25_q), .clk(in_4));  // open: clr
  Register #(.width(32)) register_26 (.D(dataWrite), .en(and_26_out), .Q(register_26_q), .clk(in_4));  // open: clr
  Register #(.width(32)) register_27 (.D(dataWrite), .en(and_27_out), .Q(register_27_q), .clk(in_4));  // open: clr
  Register #(.width(32)) register_28 (.D(dataWrite), .en(and_28_out), .Q(register_28_q), .clk(in_4));  // open: clr
  Register #(.width(32)) register_29 (.D(dataWrite), .en(and_29_out), .Q(register_29_q), .clk(in_4));  // open: clr
  Register #(.width(32)) register_30 (.D(dataWrite), .en(and_30_out), .Q(register_30_q), .clk(in_4));  // open: clr
  Register #(.width(32)) register_31 (.D(dataWrite), .en(and_31_out), .Q(register_31_q), .clk(in_4));  // open: clr
  Register #(.width(32)) register_32 (.D(dataWrite), .en(and_32_out), .Q(register_32_q), .clk(in_4));  // open: clr
  Multiplexer #(.select(5), .width(32)) multiplexer_1 (
    .in0(register_1_q), .in1(register_2_q), .in2(register_3_q), .in3(register_4_q), .in4(register_5_q),
    .in5(register_6_q), .in6(register_7_q), .in7(register_8_q), .in8(register_9_q), .in9(register_10_q),
    .in10(register_11_q), .in11(register_12_q), .in12(register_13_q), .in13(register_14_q),
    .in14(register_15_q), .in15(register_16_q), .in16(register_17_q), .in17(register_18_q),
    .in18(register_19_q), .in19(register_20_q), .in20(register_21_q), .in21(register_22_q),
    .in22(register_23_q), .in23(register_24_q), .in24(register_25_q), .in25(register_26_q),
    .in26(register_27_q), .in27(register_28_q), .in28(register_29_q), .in29(register_30_q),
    .in30(register_31_q), .in31(register_32_q), .out(regRead1), .sel(readNum_1));  // open: en
  Multiplexer #(.select(5), .width(32)) multiplexer_2 (
    .in0(register_1_q), .in1(register_2_q), .in2(register_3_q), .in3(register_4_q), .in4(register_5_q),
    .in5(register_6_q), .in6(register_7_q), .in7(register_8_q), .in8(register_9_q), .in9(register_10_q),
    .in10(register_11_q), .in11(register_12_q), .in12(register_13_q), .in13(register_14_q),
    .in14(register_15_q), .in15(register_16_q), .in16(register_17_q), .in17(register_18_q),
    .in18(register_19_q), .in19(register_20_q), .in20(register_21_q), .in21(register_22_q),
    .in22(register_23_q), .in23(register_24_q), .in24(register_25_q), .in25(register_26_q),
    .in26(register_27_q), .in27(register_28_q), .in28(register_29_q), .in29(register_30_q),
    .in30(register_31_q), .in31(register_32_q), .out(regRead2), .sel(readNum_2));  // open: en
endmodule

module ALU (
  input  [31:0] Value1,
  input  [31:0] Value2,
  input  [2:0] in_3,
  output [31:0] result
);

  wire [31:0] adder_1_out, and_1_out, multiplier_1_out, or_1_out, subtractor_1_out;

  Adder #(.width(32)) adder_1 (.a(Value1), .b(Value2), .out(adder_1_out));  // open: cin, cout
  Subtractor #(.width(32)) subtractor_1 (.a(Value1), .b(Value2), .out(subtractor_1_out));  // open: bin, bout
  Multiplier #(.width(32)) multiplier_1 (.a(Value1), .b(Value2), .out(multiplier_1_out));  // open: cin, cout
  assign and_1_out = Value1 & Value2;  // AND_Gate and_1, 32 bits wide
  assign or_1_out = Value1 | Value2;  // OR_Gate or_1, 32 bits wide
  Multiplexer #(.select(3), .width(32)) multiplexer_1 (
    .in0(adder_1_out), .in1(subtractor_1_out), .in2(or_1_out), .in4(and_1_out), .in5(or_1_out),
    .in6(and_1_out), .in7(multiplier_1_out), .out(result), .sel(in_3));  // open: in3, en
endmodule

module Control_Unit (
  input  [31:0] Instruction,
  output RegDST,
  output RegWrite,
  output [2:0] out_4,
  output ALUSrc,
  output jump
);

  wire AddI_out, and_1_out, and_2_out, and_3_out, and_6_out, AndI_out, comparator_1_eq, not_1_out, not_2_out,
       not_3_out, not_4_out, not_5_out, not_6_out, not_7_out, not_8_out, not_9_out, not_10_out, not_11_out,
       not_12_out, not_13_out, not_14_out, not_15_out, not_16_out, not_17_out, not_18_out, not_19_out,
       not_20_out, not_21_out, not_22_out, not_23_out, not_24_out, not_25_out, not_26_out, not_27_out,
       not_28_out, not_29_out, not_30_out, not_31_out, not_32_out, not_33_out, not_34_out, not_35_out,
       not_36_out, not_37_out, not_38_out, or_3_out, OrI_out, SubI_out;
  wire [2:0] and_5_out, multiplexer_2_out;

  not not_1 (not_1_out, Instruction[26]);
  not not_2 (not_2_out, Instruction[27]);
  not not_3 (not_3_out, Instruction[28]);
  not not_4 (not_4_out, Instruction[30]);
  not not_5 (not_5_out, Instruction[31]);
  not not_6 (not_6_out, Instruction[27]);
  not not_7 (not_7_out, Instruction[28]);
  not not_8 (not_8_out, Instruction[30]);
  not not_9 (not_9_out, Instruction[31]);
  not not_10 (not_10_out, Instruction[26]);
  not not_11 (not_11_out, Instruction[27]);
  not not_12 (not_12_out, Instruction[30]);
  not not_13 (not_13_out, Instruction[31]);
  not not_14 (not_14_out, Instruction[26]);
  not not_15 (not_15_out, Instruction[28]);
  not not_16 (not_16_out, Instruction[29]);
  not not_17 (not_17_out, Instruction[30]);
  not not_18 (not_18_out, Instruction[31]);
  not not_19 (not_19_out, Instruction[26]);
  not not_20 (not_20_out, Instruction[27]);
  not not_21 (not_21_out, Instruction[28]);
  not not_22 (not_22_out, Instruction[29]);
  not not_23 (not_23_out, Instruction[30]);
  not not_24 (not_24_out, Instruction[31]);
  not not_25 (not_25_out, Instruction[27]);
  not not_26 (not_26_out, Instruction[30]);
  not not_27 (not_27_out, Instruction[31]);
  and R_Type (RegDST, not_19_out, not_20_out, not_21_out, not_22_out, not_23_out, not_24_out);
  and AddI (AddI_out, not_1_out, not_2_out, not_3_out, Instruction[29], not_4_out, not_5_out);
  and SubI (SubI_out, Instruction[26], not_6_out, not_7_out, Instruction[29], not_8_out, not_9_out);
  and AndI (AndI_out, not_10_out, not_11_out, Instruction[28], Instruction[29], not_12_out, not_13_out);
  and OrI (OrI_out, Instruction[26], not_25_out, Instruction[28], Instruction[29], not_26_out, not_27_out);
  and J (jump, not_14_out, Instruction[27], not_15_out, not_16_out, not_17_out, not_18_out);
  not not_28 (not_28_out, Instruction[4]);
  or or_1 (RegWrite, RegDST, AddI_out, OrI_out, SubI_out, AndI_out);
  or or_2 (ALUSrc, AddI_out, OrI_out, SubI_out, AndI_out);
  not not_29 (not_29_out, Instruction[2]);
  not not_30 (not_30_out, Instruction[1]);
  not not_31 (not_31_out, Instruction[3]);
  not not_32 (not_32_out, Instruction[4]);
  not not_33 (not_33_out, Instruction[1]);
  not not_34 (not_34_out, Instruction[0]);
  not not_35 (not_35_out, Instruction[2]);
  and and_1 (and_1_out, Instruction[1], not_29_out, not_31_out);
  and and_2 (and_2_out, not_30_out, Instruction[2], not_31_out);
  not not_36 (not_36_out, Instruction[0]);
  and and_3 (and_3_out, not_32_out, not_36_out, Instruction[5]);
  not not_37 (not_37_out, Instruction[4]);
  and and_4 (and_5_out[2], not_34_out, Instruction[1], not_35_out, not_28_out, Instruction[5]);
  or or_3 (or_3_out, and_1_out, and_2_out);
  not not_38 (not_38_out, Instruction[3]);
  and and_5 (and_5_out[0], or_3_out, and_3_out);
  and and_6 (and_6_out, Instruction[0], not_33_out, Instruction[2], not_38_out, not_37_out, Instruction[5]);
  Multiplexer #(.width(3)) multiplexer_1 (
    .in0(Instruction[28:26]), .in1(multiplexer_2_out), .out(out_4), .sel(RegDST));  // open: en
  or or_4 (and_5_out[1], and_5_out[0], and_6_out);
  Comparator #(.width(6)) comparator_1 (.a(6'b011000), .b(Instruction[5:0]), .eq(comparator_1_eq));  // open: gt, lt
  Multiplexer #(.width(3)) multiplexer_2 (
    .in0(and_5_out), .in1(3'b111), .out(multiplexer_2_out), .sel(comparator_1_eq));  // open: en

  // Notes on the sheet:
  //   Opcode
  //   ALU ctr [0]
  //   ALU ctr [2]
  //   ALU ctr
  //   ALU ctr [1]
endmodule
