// Logisim project RegisterFile Design.circ as structural Verilog: 1 circuit, main circuit main
module main (
  input  [31:0] dataWrite,
  input  [4:0] regNum,
  input  regWrite,
  input  [4:0] readNum_1,
  input  [4:0] readNum_2,
  output [31:0] regRead1,
  output [31:0] regRead2
);

  wire and_1_out, and_2_out, and_3_out, and_4_out, and_5_out, and_6_out, and_7_out, and_8_out, and_9_out,
       and_10_out, and_11_out, and_12_out, and_13_out, and_14_out, and_15_out, and_16_out, and_17_out,
       and_18_out, and_19_out, and_20_out, and_21_out, and_22_out, and_23_out, and_24_out, and_25_out,
       and_26_out, and_27_out, and_28_out, and_29_out, and_30_out, and_31_out, and_32_out, clock_out,
       decoder_1_out0, decoder_1_out1, decoder_1_out2, decoder_1_out3, decoder_1_out4, decoder_1_out5,
       decoder_1_out6, decoder_1_out7, decoder_1_out8, decoder_1_out9, decoder_1_out10, decoder_1_out11,
       decoder_1_out12, decoder_1_out13, decoder_1_out14, decoder_1_out15, decoder_1_out16, decoder_1_out17,
       decoder_1_out18, decoder_1_out19, decoder_1_out20, decoder_1_out21, decoder_1_out22, decoder_1_out23,
       decoder_1_out24, decoder_1_out25, decoder_1_out26, decoder_1_out27, decoder_1_out28, decoder_1_out29,
       decoder_1_out30, decoder_1_out31;
  wire [31:0] register_1_q, register_2_q, register_3_q, register_4_q, register_5_q, register_6_q,
       register_7_q, register_8_q, register_9_q, register_10_q, register_11_q, register_12_q, register_13_q,
       register_14_q, register_15_q, register_16_q, register_17_q, register_18_q, register_19_q,
       register_20_q, register_21_q, register_22_q, register_23_q, register_24_q, register_25_q,
       register_26_q, register_27_q, register_28_q, register_29_q, register_30_q, register_31_q,
       register_32_q;

  Decoder #(.select(5)) decoder_1 (
    .out0(decoder_1_out0), .out1(decoder_1_out1), .out2(decoder_1_out2), .out3(decoder_1_out3),
    .out4(decoder_1_out4), .out5(decoder_1_out5), .out6(decoder_1_out6), .out7(decoder_1_out7),
    .out8(decoder_1_out8), .out9(decoder_1_out9), .out10(decoder_1_out10), .out11(decoder_1_out11),
    .out12(decoder_1_out12), .out13(decoder_1_out13), .out14(decoder_1_out14), .out15(decoder_1_out15),
    .out16(decoder_1_out16), .out17(decoder_1_out17), .out18(decoder_1_out18), .out19(decoder_1_out19),
    .out20(decoder_1_out20), .out21(decoder_1_out21), .out22(decoder_1_out22), .out23(decoder_1_out23),
    .out24(decoder_1_out24), .out25(decoder_1_out25), .out26(decoder_1_out26), .out27(decoder_1_out27),
    .out28(decoder_1_out28), .out29(decoder_1_out29), .out30(decoder_1_out30), .out31(decoder_1_out31),
    .sel(regNum));  // open: en
  and and_1 (and_1_out, regWrite, decoder_1_out0);
  and and_2 (and_2_out, regWrite, decoder_1_out1);
  and and_3 (and_3_out, regWrite, decoder_1_out2);
  and and_4 (and_4_out, regWrite, decoder_1_out3);
  and and_5 (and_5_out, regWrite, decoder_1_out4);
  and and_6 (and_6_out, regWrite, decoder_1_out5);
  and and_7 (and_7_out, regWrite, decoder_1_out6);
  and and_8 (and_8_out, regWrite, decoder_1_out7);
  Register #(.width(32)) register_1 (.D(dataWrite), .en(and_1_out), .Q(register_1_q), .clk(clock_out));  // open: clr
  Register #(.width(32)) register_2 (.D(dataWrite), .en(and_2_out), .Q(register_2_q), .clk(clock_out));  // open: clr
  Register #(.width(32)) register_3 (.D(dataWrite), .en(and_3_out), .Q(register_3_q), .clk(clock_out));  // open: clr
  Register #(.width(32)) register_4 (.D(dataWrite), .en(and_4_out), .Q(register_4_q), .clk(clock_out));  // open: clr
  Register #(.width(32)) register_5 (.D(dataWrite), .en(and_5_out), .Q(register_5_q), .clk(clock_out));  // open: clr
  Register #(.width(32)) register_6 (.D(dataWrite), .en(and_6_out), .Q(register_6_q), .clk(clock_out));  // open: clr
  Register #(.width(32)) register_7 (.D(dataWrite), .en(and_7_out), .Q(register_7_q), .clk(clock_out));  // open: clr
  Register #(.width(32)) register_8 (.D(dataWrite), .en(and_8_out), .Q(register_8_q), .clk(clock_out));  // open: clr
  Clock clock (.out(clock_out));
  and and_9 (and_9_out, regWrite, decoder_1_out8);
  and and_10 (and_10_out, regWrite, decoder_1_out9);
  and and_11 (and_11_out, regWrite, decoder_1_out10);
  and and_12 (and_12_out, regWrite, decoder_1_out11);
  and and_13 (and_13_out, regWrite, decoder_1_out12);
  and and_14 (and_14_out, regWrite, decoder_1_out13);
  and and_15 (and_15_out, regWrite, decoder_1_out14);
  and and_16 (and_16_out, regWrite, decoder_1_out15);
  Register #(.width(32)) register_9 (.D(dataWrite), .en(and_9_out), .Q(register_9_q), .clk(clock_out));  // open: clr
  Register #(.width(32)) register_10 (.D(dataWrite), .en(and_10_out), .Q(register_10_q), .clk(clock_out));  // open: clr
  Register #(.width(32)) register_11 (.D(dataWrite), .en(and_11_out), .Q(register_11_q), .clk(clock_out));  // open: clr
  Register #(.width(32)) register_12 (.D(dataWrite), .en(and_12_out), .Q(register_12_q), .clk(clock_out));  // open: clr
  Register #(.width(32)) register_13 (.D(dataWrite), .en(and_13_out), .Q(register_13_q), .clk(clock_out));  // open: clr
  Register #(.width(32)) register_14 (.D(dataWrite), .en(and_14_out), .Q(register_14_q), .clk(clock_out));  // open: clr
  Register #(.width(32)) register_15 (.D(dataWrite), .en(and_15_out), .Q(register_15_q), .clk(clock_out));  // open: clr
  Register #(.width(32)) register_16 (.D(dataWrite), .en(and_16_out), .Q(register_16_q), .clk(clock_out));  // open: clr
  and and_17 (and_17_out, regWrite, decoder_1_out16);
  and and_18 (and_18_out, regWrite, decoder_1_out17);
  and and_19 (and_19_out, regWrite, decoder_1_out18);
  and and_20 (and_20_out, regWrite, decoder_1_out19);
  and and_21 (and_21_out, regWrite, decoder_1_out20);
  and and_22 (and_22_out, regWrite, decoder_1_out21);
  and and_23 (and_23_out, regWrite, decoder_1_out22);
  and and_24 (and_24_out, regWrite, decoder_1_out23);
  Register #(.width(32)) register_17 (.D(dataWrite), .en(and_17_out), .Q(register_17_q), .clk(clock_out));  // open: clr
  Register #(.width(32)) register_18 (.D(dataWrite), .en(and_18_out), .Q(register_18_q), .clk(clock_out));  // open: clr
  Register #(.width(32)) register_19 (.D(dataWrite), .en(and_19_out), .Q(register_19_q), .clk(clock_out));  // open: clr
  Register #(.width(32)) register_20 (.D(dataWrite), .en(and_20_out), .Q(register_20_q), .clk(clock_out));  // open: clr
  Register #(.width(32)) register_21 (.D(dataWrite), .en(and_21_out), .Q(register_21_q), .clk(clock_out));  // open: clr
  Register #(.width(32)) register_22 (.D(dataWrite), .en(and_22_out), .Q(register_22_q), .clk(clock_out));  // open: clr
  Register #(.width(32)) register_23 (.D(dataWrite), .en(and_23_out), .Q(register_23_q), .clk(clock_out));  // open: clr
  Register #(.width(32)) register_24 (.D(dataWrite), .en(and_24_out), .Q(register_24_q), .clk(clock_out));  // open: clr
  and and_25 (and_25_out, regWrite, decoder_1_out24);
  and and_26 (and_26_out, regWrite, decoder_1_out25);
  and and_27 (and_27_out, regWrite, decoder_1_out26);
  and and_28 (and_28_out, regWrite, decoder_1_out27);
  and and_29 (and_29_out, regWrite, decoder_1_out28);
  and and_30 (and_30_out, regWrite, decoder_1_out29);
  and and_31 (and_31_out, regWrite, decoder_1_out30);
  and and_32 (and_32_out, regWrite, decoder_1_out31);
  Register #(.width(32)) register_25 (.D(dataWrite), .en(and_25_out), .Q(register_25_q), .clk(clock_out));  // open: clr
  Register #(.width(32)) register_26 (.D(dataWrite), .en(and_26_out), .Q(register_26_q), .clk(clock_out));  // open: clr
  Register #(.width(32)) register_27 (.D(dataWrite), .en(and_27_out), .Q(register_27_q), .clk(clock_out));  // open: clr
  Register #(.width(32)) register_28 (.D(dataWrite), .en(and_28_out), .Q(register_28_q), .clk(clock_out));  // open: clr
  Register #(.width(32)) register_29 (.D(dataWrite), .en(and_29_out), .Q(register_29_q), .clk(clock_out));  // open: clr
  Register #(.width(32)) register_30 (.D(dataWrite), .en(and_30_out), .Q(register_30_q), .clk(clock_out));  // open: clr
  Register #(.width(32)) register_31 (.D(dataWrite), .en(and_31_out), .Q(register_31_q), .clk(clock_out));  // open: clr
  Register #(.width(32)) register_32 (.D(dataWrite), .en(and_32_out), .Q(register_32_q), .clk(clock_out));  // open: clr
  Multiplexer #(.select(5), .width(32)) multiplexer_1 (
    .in0(register_1_q), .in1(register_2_q), .in2(register_3_q), .in3(register_4_q), .in4(register_5_q),
    .in5(register_6_q), .in6(register_7_q), .in7(register_8_q), .in8(register_9_q), .in9(register_10_q),
    .in10(register_11_q), .in11(register_12_q), .in12(register_13_q), .in13(register_14_q),
    .in14(register_15_q), .in15(register_16_q), .in16(register_17_q), .in17(register_18_q),
    .in18(register_19_q), .in19(register_20_q), .in20(register_21_q), .in21(register_22_q),
    .in22(register_23_q), .in23(register_24_q), .in24(register_25_q), .in25(register_26_q),
    .in26(register_27_q), .in27(register_28_q), .in28(register_29_q), .in29(register_30_q),
    .in30(register_31_q), .in31(register_32_q), .out(regRead1), .sel(readNum_1));  // open: en
  Multiplexer #(.select(5), .width(32)) multiplexer_2 (
    .in0(register_1_q), .in1(register_2_q), .in2(register_3_q), .in3(register_4_q), .in4(register_5_q),
    .in5(register_6_q), .in6(register_7_q), .in7(register_8_q), .in8(register_9_q), .in9(register_10_q),
    .in10(register_11_q), .in11(register_12_q), .in12(register_13_q), .in13(register_14_q),
    .in14(register_15_q), .in15(register_16_q), .in16(register_17_q), .in17(register_18_q),
    .in18(register_19_q), .in19(register_20_q), .in20(register_21_q), .in21(register_22_q),
    .in22(register_23_q), .in23(register_24_q), .in24(register_25_q), .in25(register_26_q),
    .in26(register_27_q), .in27(register_28_q), .in28(register_29_q), .in29(register_30_q),
    .in30(register_31_q), .in31(register_32_q), .out(regRead2), .sel(readNum_2));  // open: en
endmodule
